// Logisim project stack_logical_normal.circ as structural Verilog: 15 circuits, main circuit main
module main (
  input  CLK,
  input  RESET,
  input  [1:0] COMMAND,
  input  [2:0] INDEX,
  input  [3:0] IO_DATA_in,
  output [3:0] IO_DATA_out
);

  wire [3:0] stack_1_d0, stack_1_d1, stack_1_d2, stack_1_d3, stack_1_d4;

  // Probe on stack_1_d0
  stack stack_1 (
    .CLK(CLK), .RESET(RESET), .COMMAND(COMMAND), .INDEX(INDEX), .IO_DATA_in(IO_DATA_in), .d0(stack_1_d0),
    .d1(stack_1_d1), .d2(stack_1_d2), .d3(stack_1_d3), .d4(stack_1_d4), .IO_DATA_out(IO_DATA_out));
  // Probe on stack_1_d1
  // Probe on stack_1_d2
  // Probe on stack_1_d3
  // Probe on stack_1_d4
endmodule

module stack (
  input  CLK,
  input  RESET,
  input  [1:0] COMMAND,
  input  [2:0] INDEX,
  input  [3:0] IO_DATA_in,
  output [3:0] d0,
  output [3:0] d1,
  output [3:0] d2,
  output [3:0] d3,
  output [3:0] d4,
  output [3:0] IO_DATA_out
);

  wire and_4_out, and_5_out, and_6_out, and_7_out, and_8_out, and_9_out, and_10_out, and_11_out, and_12_out,
       and_13_out, decoder_1_q1, decoder_1_q2, decoder_1_q3, decoder_2_q0, decoder_2_q1, decoder_2_q2,
       decoder_2_q3, decoder_2_q4, nor_1_out, not_1_out, or_1_out, read_1_q0, read_1_q1, read_1_q2,
       read_1_q3, read_2_q0, read_2_q1, read_2_q2, read_2_q3, read_3_q0, read_3_q1, read_3_q2, read_3_q3,
       read_4_q0, read_4_q1, read_4_q2, read_4_q3, read_5_q0, read_5_q1, read_5_q2, read_5_q3;
  wire [2:0] and_1_out, increment_1_newind, pointer_1_q, sum3_1_q;
  wire [3:0] or_2_out;

  and and_1 (and_1_out[0], decoder_1_q3, INDEX[0]);
  and and_2 (and_1_out[1], decoder_1_q3, INDEX[1]);
  and and_3 (and_1_out[2], decoder_1_q3, INDEX[2]);
  Decoder decoder_1 (
    .A0(COMMAND[0]), .A1(COMMAND[1]), .Q1(decoder_1_q1), .Q2(decoder_1_q2), .Q3(decoder_1_q3));  // open: A2, Q0, Q4
  Pointer pointer_1 (.C(CLK), .reset(RESET), .needInc(decoder_1_q1), .needDec(decoder_1_q2), .Q(pointer_1_q));
  nor nor_1 (nor_1_out, decoder_1_q3, decoder_1_q2);
  Increment increment_1 (.IND(pointer_1_q), .need(decoder_1_q2), .newIND(increment_1_newind));
  or or_1 (or_1_out, ~CLK, nor_1_out);  // OR_Gate
  Sum3 sum3_1 (.A0(increment_1_newind), .A1(and_1_out), .Q(sum3_1_q));
  Decoder decoder_2 (
    .A0(sum3_1_q[0]), .A1(sum3_1_q[1]), .A2(sum3_1_q[2]), .Q0(decoder_2_q0), .Q1(decoder_2_q1),
    .Q2(decoder_2_q2), .Q3(decoder_2_q3), .Q4(decoder_2_q4));
  and and_4 (and_4_out, decoder_1_q1, decoder_2_q0);
  and and_5 (and_5_out, decoder_1_q1, decoder_2_q1);
  and and_6 (and_6_out, decoder_1_q1, decoder_2_q2);
  and and_7 (and_7_out, decoder_1_q1, decoder_2_q3);
  and and_8 (and_8_out, decoder_1_q1, decoder_2_q4);
  and and_9 (and_9_out, CLK, decoder_2_q0);
  and and_10 (and_10_out, CLK, decoder_2_q1);
  and and_11 (and_11_out, CLK, decoder_2_q2);
  and and_12 (and_12_out, CLK, decoder_2_q3);
  and and_13 (and_13_out, CLK, decoder_2_q4);
  StackCell stackcell_1 (.RW(and_4_out), .C(and_9_out), .reset(RESET), .D(IO_DATA_in), .Q(d0));
  StackCell stackcell_2 (.RW(and_5_out), .C(and_10_out), .reset(RESET), .D(IO_DATA_in), .Q(d1));
  StackCell stackcell_3 (.RW(and_6_out), .C(and_11_out), .reset(RESET), .D(IO_DATA_in), .Q(d2));
  StackCell stackcell_4 (.RW(and_7_out), .C(and_12_out), .reset(RESET), .D(IO_DATA_in), .Q(d3));
  StackCell stackcell_5 (.RW(and_8_out), .C(and_13_out), .reset(RESET), .D(IO_DATA_in), .Q(d4));
  Read read_1 (.A(d0), .R(decoder_2_q0), .Q0(read_1_q0), .Q1(read_1_q1), .Q2(read_1_q2), .Q3(read_1_q3));
  Read read_2 (.A(d1), .R(decoder_2_q1), .Q0(read_2_q0), .Q1(read_2_q1), .Q2(read_2_q2), .Q3(read_2_q3));
  Read read_3 (.A(d2), .R(decoder_2_q2), .Q0(read_3_q0), .Q1(read_3_q1), .Q2(read_3_q2), .Q3(read_3_q3));
  Read read_4 (.A(d3), .R(decoder_2_q3), .Q0(read_4_q0), .Q1(read_4_q1), .Q2(read_4_q2), .Q3(read_4_q3));
  Read read_5 (.A(d4), .R(decoder_2_q4), .Q0(read_5_q0), .Q1(read_5_q1), .Q2(read_5_q2), .Q3(read_5_q3));
  or or_2 (or_2_out[0], read_1_q0, read_2_q0, read_3_q0, read_4_q0, read_5_q0);
  or or_3 (or_2_out[1], read_1_q1, read_2_q1, read_3_q1, read_4_q1, read_5_q1);
  or or_4 (or_2_out[2], read_1_q2, read_2_q2, read_3_q2, read_4_q2, read_5_q2);
  or or_5 (or_2_out[3], read_1_q3, read_2_q3, read_3_q3, read_4_q3, read_5_q3);
  not not_1 (not_1_out, or_1_out);
  // Transmission_Gate #(.width(4)) transmission_1: pin names not known; wires that end beside it: or_2_out, or_1_out, not_1_out, IO_DATA_in

  assign IO_DATA_out = IO_DATA_in;
endmodule

module StackCell (
  input  RW,
  input  C,
  input  reset,
  input  [3:0] D,
  output [3:0] Q
);

  wire and_1_out;

  and and_1 (and_1_out, RW, C);
  Dtrigger dtrigger_1 (.C(and_1_out), .D(D[0]), .reset(reset), .Q(Q[0]));
  Dtrigger dtrigger_2 (.C(and_1_out), .D(D[1]), .reset(reset), .Q(Q[1]));
  Dtrigger dtrigger_3 (.C(and_1_out), .D(D[2]), .reset(reset), .Q(Q[2]));
  Dtrigger dtrigger_4 (.C(and_1_out), .D(D[3]), .reset(reset), .Q(Q[3]));
endmodule

module RStrigger (
  input  R,
  input  C,
  input  S,
  input  reset,
  output Q
);

  wire and_1_out, and_2_out, nor_2_out, or_1_out, por_1_out;

  and and_1 (and_1_out, R, C);
  and and_2 (and_2_out, C, S);
  nor nor_1 (Q, and_1_out, or_1_out);
  nor nor_2 (nor_2_out, Q, and_2_out);
  or or_1 (or_1_out, nor_2_out, reset, por_1_out);
  POR por_1 (.out(por_1_out));
endmodule

module Dtrigger (
  input  C,
  input  D,
  input  reset,
  output Q
);

  wire not_1_out;

  not not_1 (not_1_out, D);
  RStrigger rstrigger_1 (.R(not_1_out), .C(C), .S(D), .reset(reset), .Q(Q));
endmodule

module Decoder (
  input  A0,
  input  A1,
  input  A2,
  output Q0,
  output Q1,
  output Q2,
  output Q3,
  output Q4
);

  and and_1 (Q0, ~A0, ~A1, ~A2);  // AND_Gate
  and and_2 (Q1, A0, ~A1, ~A2);  // AND_Gate
  and and_3 (Q2, ~A0, A1, ~A2);  // AND_Gate
  and and_4 (Q3, A0, A1, ~A2);  // AND_Gate
  and and_5 (Q4, ~A0, ~A1, A2);  // AND_Gate
endmodule

module HalfSummator (
  input  A0,
  input  A1,
  output C,
  output S
);

  and and_1 (C, A0, A1);
  xor xor_1 (S, A1, A0);
endmodule

module Summator (
  input  A0,
  input  A1,
  input  A2,
  output S,
  output C
);

  wire halfsummator_1_c, halfsummator_1_s, halfsummator_2_c;

  HalfSummator halfsummator_1 (.A0(A1), .A1(A2), .C(halfsummator_1_c), .S(halfsummator_1_s));
  HalfSummator halfsummator_2 (.A0(A0), .A1(halfsummator_1_s), .C(halfsummator_2_c), .S(S));
  xor xor_1 (C, halfsummator_2_c, halfsummator_1_c);
endmodule

module Sum3 (
  input  [2:0] A0,
  input  [2:0] A1,
  output [2:0] Q
);

  wire halfsummator_1_c, halfsummator_1_s, summator_1_c, summator_1_s, summator_2_c, summator_2_s;

  HalfSummator halfsummator_1 (.A0(A0[0]), .A1(A1[0]), .C(halfsummator_1_c), .S(halfsummator_1_s));
  Summator summator_1 (.A0(A0[1]), .A1(A1[1]), .A2(halfsummator_1_c), .S(summator_1_s), .C(summator_1_c));
  Summator summator_2 (.A0(A0[2]), .A1(A1[2]), .A2(summator_1_c), .S(summator_2_s), .C(summator_2_c));
  Mod5 mod5_1 (.A0(summator_2_c), .A1(summator_2_s), .A2(summator_1_s), .A3(halfsummator_1_s), .Q(Q));
endmodule

module Mod5 (
  input  A0,
  input  A1,
  input  A2,
  input  A3,
  output [2:0] Q
);

  wire and_1_out, and_2_out, and_3_out, and_4_out, and_5_out, and_6_out, and_7_out, and_8_out, and_9_out;

  and and_1 (and_1_out, A1, ~A2, ~A3);  // AND_Gate
  and and_2 (and_2_out, A0, ~A2, A3);  // AND_Gate
  and and_3 (and_3_out, A0, ~A2, ~A3);  // AND_Gate
  and and_4 (and_4_out, ~A0, A2, A3);  // AND_Gate
  and and_5 (and_5_out, ~A0, ~A1, A2);  // AND_Gate
  and and_6 (and_6_out, A0, ~A2, ~A3);  // AND_Gate
  and and_7 (and_7_out, ~A1, A2, A3);  // AND_Gate
  and and_8 (and_8_out, A1, A2, ~A3);  // AND_Gate
  and and_9 (and_9_out, ~A0, ~A1, A3);  // AND_Gate
  or or_1 (Q[2], and_1_out, and_2_out);
  or or_2 (Q[1], and_3_out, and_4_out, and_5_out);
  or or_3 (Q[0], and_6_out, and_7_out, and_8_out, and_9_out);
endmodule

module Increment (
  input  [2:0] IND,
  input  need,
  output [2:0] newIND
);

  wire [2:2] and_1_out;

  and and_1 (and_1_out[2], need, 1'b1);
  Sum3 sum3_1 (.A0(IND), .A1({and_1_out[2], 2'b00}), .Q(newIND));
endmodule

module Decrement (
  input  [2:0] IND,
  input  need,
  output [2:0] newIND
);

  Sum3 sum3_1 (.A0(IND), .A1({2'b00, need}), .Q(newIND));
endmodule

module Pointer (
  input  C,
  input  reset,
  input  needInc,
  input  needDec,
  output [2:0] Q
);

  wire and_1_out, not_1_out, or_1_out;
  wire [2:0] increment_1_newind, pointercell_1_q, pointercell_2_q;

  or or_1 (or_1_out, needInc, needDec);
  Increment increment_1 (.IND(pointercell_2_q), .need(needInc), .newIND(increment_1_newind));
  Decrement decrement_1 (.IND(increment_1_newind), .need(needDec), .newIND(Q));
  and and_1 (and_1_out, or_1_out, C);
  not not_1 (not_1_out, and_1_out);
  PointerCell pointercell_1 (.C(and_1_out), .reset(reset), .D(Q), .Q(pointercell_1_q));
  PointerCell pointercell_2 (.C(not_1_out), .reset(reset), .D(pointercell_1_q), .Q(pointercell_2_q));
endmodule

module PointerCell (
  input  C,
  input  reset,
  input  [2:0] D,
  output [2:0] Q
);

  Dtrigger dtrigger_1 (.C(C), .D(D[0]), .reset(reset), .Q(Q[0]));
  Dtrigger dtrigger_2 (.C(C), .D(D[1]), .reset(reset), .Q(Q[1]));
  Dtrigger dtrigger_3 (.C(C), .D(D[2]), .reset(reset), .Q(Q[2]));
endmodule

module Read (
  input  [3:0] A,
  input  R,
  output Q0,
  output Q1,
  output Q2,
  output Q3
);

  and and_1 (Q0, R, A[0]);
  and and_2 (Q1, R, A[1]);
  and and_3 (Q2, R, A[2]);
  and and_4 (Q3, R, A[3]);
endmodule
